# Fritzing sketch Aufbau (saved by Fritzing 0.9.3b)
breadboards: 1

parts:
  Bauteil1 = Arduino Mega 2560 (Rev3)
  S1 = Round Pushbutton
  S2 = Round Pushbutton
  S3 = Round Pushbutton
  S4 = Round Pushbutton
  S5 = Round Pushbutton
  S6 = Round Pushbutton
  LED1 = LED - 3mm [color="Red (633nm)" package="3 mm [THT]"]
  LED2 = LED - 3mm [color="Red (633nm)" package="3 mm [THT]"]
  LED3 = LED - 3mm [color="Red (633nm)" package="3 mm [THT]"]
  LED4 = LED - 3mm [color="Red (633nm)" package="3 mm [THT]"]
  LED5 = LED - 3mm [color="Red (633nm)" package="3 mm [THT]"]
  LED6 = LED - 3mm [color="Red (633nm)" package="3 mm [THT]"]
  ULN1 = Darlington Driver [package=dil18]

nets:
  N1: Bauteil1.5V, LED1.anode, LED2.anode, LED3.anode, LED4.anode, LED5.anode, LED6.anode, ULN1.10
  N2: Bauteil1.GND, S1.leg1, S2.leg1, S3.leg1, S4.leg1, S5.leg1, S6.leg1, ULN1.9
  N3: LED1.cathode, ULN1.15
  N4: LED2.cathode, ULN1.16
  N5: LED3.cathode, ULN1.14
  N6: LED4.cathode, ULN1.13
  N7: LED5.cathode, ULN1.12
  N8: LED6.cathode, ULN1.11
